// Logisim project Lab2 (Logic Gates) - Logisim.circ as structural Verilog: 1 circuit, main circuit main
module main (
  input  A,
  input  A_2,
  input  B,
  input  B_2,
  input  A_3,
  input  A_4,
  input  B_3,
  input  B_4,
  input  A_5,
  input  A_6,
  input  B_5,
  input  A_7,
  input  B_6,
  output C,
  output C_2,
  output C_3,
  output C_4,
  output C_5,
  output C_6,
  output C_7
);

  and and_1 (C, A, B);
  or or_1 (C_3, A_3, B_3);
  not not_1 (C_5, A_6);
  xnor xnor_1 (C_7, A_7, B_6);
  nand nand_1 (C_2, A_2, B_2);
  nor nor_1 (C_4, A_4, B_4);
  xor xor_1 (C_6, A_5, B_5);

  // Notes on the sheet:
  //   AND Gate
  //   OR Gate
  //   NOT Gate
  //   Humair Shoukat 2302
  //   XNOR Gate
  //   NOR Gate
  //   NAND Gate
  //   XOR Gate
endmodule
