// Logisim project Lab3 (DeMorgan's Law) - Logisim.circ as structural Verilog: 1 circuit, main circuit main
module main (
  input  A,
  input  B,
  input  A_2,
  input  B_2,
  output LHS,
  output RHS,
  output LHS_2,
  output RHS_2
);

  wire A_B_2_out, A_B_out, A_prime_2_out, A_prime_out, B_prime_2_out, B_prime_out;

  not A_prime (A_prime_out, A);
  not B_prime (B_prime_out, B);
  not A_prime_2 (A_prime_2_out, A_2);
  not B_prime_2 (B_prime_2_out, A_2);
  or A_B (A_B_out, A, B);
  and A_B_2 (A_B_2_out, A_2, B_2);
  not A_B__prime (LHS, A_B_out);
  and A_prime_B_prime (RHS, A_prime_out, B_prime_out);
  not A_B__prime_2 (LHS_2, A_B_2_out);
  or A_prime_B_prime_2 (RHS_2, A_prime_2_out, B_prime_2_out);

  // Notes on the sheet:
  //   (A)
  //   (B)
  //   De Morgan's Law
  //   Humair Shoukat 2302
endmodule
