// Logisim project Lab4 (Distributive Law) - Logisim.circ as structural Verilog: 1 circuit, main circuit main
module main (
  input  A,
  input  B,
  input  C,
  output LHS,
  output RHS
);

  wire A_B_out, A_C_out, B_C_out;

  or B_C (B_C_out, B, C);
  and A_B (A_B_out, A, B);
  and A_C (A_C_out, A, C);
  and A_B_C (LHS, A, B_C_out);
  or AB_AC (RHS, A_B_out, A_C_out);

  // Notes on the sheet:
  //   Distributive Law
  //   Humair Shoukat 2302
endmodule
